// Logisim project procesador_monociclo.circ as structural Verilog
module alu32 (
  input  [31:0] A,
  input  [31:0] B,
  input  [2:0] OP,
  output [31:0] R,
  output Z
);

  wire comparator_1_lt;
  wire [31:0] adder_1_out, and_1_out, bit_extender_1_out, nor_1_out, or_1_out, subtractor_1_out;

  assign and_1_out = A & B;  // AND_Gate and_1, 32 bits wide
  assign or_1_out = A | B;  // OR_Gate or_1, 32 bits wide
  assign nor_1_out = ~(A | B);  // NOR_Gate nor_1, 32 bits wide
  Adder #(.width(32)) adder_1 (.a(A), .b(B), .out(adder_1_out));  // open: cin, cout
  Subtractor #(.width(32)) subtractor_1 (.a(A), .b(B), .out(subtractor_1_out));  // open: bin, bout
  Comparator #(.width(32)) comparator_1 (.a(A), .b(B), .lt(comparator_1_lt));  // open: gt, eq
  assign bit_extender_1_out = {{31{1'b0}}, comparator_1_lt};  // Bit_Extender bit_extender_1
  Multiplexer #(.select(3), .width(32)) multiplexer_1 (
    .in0(adder_1_out), .in1(subtractor_1_out), .in2(and_1_out), .in3(or_1_out), .in4(nor_1_out),
    .in5(bit_extender_1_out), .in6({32{1'b0}}), .in7({32{1'b0}}), .out(R), .sel(OP));
  Comparator #(.mode("unsigned"), .width(32)) comparator_2 (.a(R), .b({32{1'b0}}), .eq(Z));  // open: gt, lt
endmodule

module banco_registros (
  input  [4:0] rs,
  input  [4:0] rt,
  input  [4:0] wr,
  input  [31:0] wd,
  input  we,
  input  clk,
  input  rst,
  output [31:0] A,
  output [31:0] B,
  output [31:0] R0,
  output [31:0] R1,
  output [31:0] R2,
  output [31:0] R3,
  output [31:0] R4,
  output [31:0] R5,
  output [31:0] R6,
  output [31:0] R7,
  output [31:0] R8,
  output [31:0] R9,
  output [31:0] R10,
  output [31:0] R11,
  output [31:0] R12,
  output [31:0] R13,
  output [31:0] R14,
  output [31:0] R15,
  output [31:0] R16,
  output [31:0] R17,
  output [31:0] R18,
  output [31:0] R19,
  output [31:0] R20,
  output [31:0] R21,
  output [31:0] R22,
  output [31:0] R23,
  output [31:0] R24,
  output [31:0] R25,
  output [31:0] R26,
  output [31:0] R27,
  output [31:0] R28,
  output [31:0] R29,
  output [31:0] R30,
  output [31:0] R31
);

  wire decoder_1_out1, decoder_1_out2, decoder_1_out3, decoder_1_out4, decoder_1_out5, decoder_1_out6,
       decoder_1_out7, decoder_1_out8, decoder_1_out9, decoder_1_out10, decoder_1_out11, decoder_1_out12,
       decoder_1_out13, decoder_1_out14, decoder_1_out15, decoder_1_out16, decoder_1_out17, decoder_1_out18,
       decoder_1_out19, decoder_1_out20, decoder_1_out21, decoder_1_out22, decoder_1_out23, decoder_1_out24,
       decoder_1_out25, decoder_1_out26, decoder_1_out27, decoder_1_out28, decoder_1_out29, decoder_1_out30,
       decoder_1_out31;

  Decoder #(.select(5)) decoder_1 (
    .out1(decoder_1_out1), .out2(decoder_1_out2), .out3(decoder_1_out3), .out4(decoder_1_out4),
    .out5(decoder_1_out5), .out6(decoder_1_out6), .out7(decoder_1_out7), .out8(decoder_1_out8),
    .out9(decoder_1_out9), .out10(decoder_1_out10), .out11(decoder_1_out11), .out12(decoder_1_out12),
    .out13(decoder_1_out13), .out14(decoder_1_out14), .out15(decoder_1_out15), .out16(decoder_1_out16),
    .out17(decoder_1_out17), .out18(decoder_1_out18), .out19(decoder_1_out19), .out20(decoder_1_out20),
    .out21(decoder_1_out21), .out22(decoder_1_out22), .out23(decoder_1_out23), .out24(decoder_1_out24),
    .out25(decoder_1_out25), .out26(decoder_1_out26), .out27(decoder_1_out27), .out28(decoder_1_out28),
    .out29(decoder_1_out29), .out30(decoder_1_out30), .out31(decoder_1_out31), .sel(wr), .en(we));  // open: out0
  Register #(.width(32)) registro0 (.D({32{1'b0}}), .en(1'b1), .Q(R0), .clk(clk), .clr(rst));
  Register #(.width(32)) registro1 (.D(wd), .en(decoder_1_out1), .Q(R1), .clk(clk), .clr(rst));
  Register #(.width(32)) registro2 (.D(wd), .en(decoder_1_out2), .Q(R2), .clk(clk), .clr(rst));
  Register #(.width(32)) registro3 (.D(wd), .en(decoder_1_out3), .Q(R3), .clk(clk), .clr(rst));
  Register #(.width(32)) registro4 (.D(wd), .en(decoder_1_out4), .Q(R4), .clk(clk), .clr(rst));
  Register #(.width(32)) registro5 (.D(wd), .en(decoder_1_out5), .Q(R5), .clk(clk), .clr(rst));
  Register #(.width(32)) registro6 (.D(wd), .en(decoder_1_out6), .Q(R6), .clk(clk), .clr(rst));
  Register #(.width(32)) registro7 (.D(wd), .en(decoder_1_out7), .Q(R7), .clk(clk), .clr(rst));
  Register #(.width(32)) registro8 (.D(wd), .en(decoder_1_out8), .Q(R8), .clk(clk), .clr(rst));
  Register #(.width(32)) registro9 (.D(wd), .en(decoder_1_out9), .Q(R9), .clk(clk), .clr(rst));
  Register #(.width(32)) registro10 (.D(wd), .en(decoder_1_out10), .Q(R10), .clk(clk), .clr(rst));
  Register #(.width(32)) registro11 (.D(wd), .en(decoder_1_out11), .Q(R11), .clk(clk), .clr(rst));
  Register #(.width(32)) registro12 (.D(wd), .en(decoder_1_out12), .Q(R12), .clk(clk), .clr(rst));
  Register #(.width(32)) registro13 (.D(wd), .en(decoder_1_out13), .Q(R13), .clk(clk), .clr(rst));
  Register #(.width(32)) registro14 (.D(wd), .en(decoder_1_out14), .Q(R14), .clk(clk), .clr(rst));
  Register #(.width(32)) registro15 (.D(wd), .en(decoder_1_out15), .Q(R15), .clk(clk), .clr(rst));
  Register #(.width(32)) registro16 (.D(wd), .en(decoder_1_out16), .Q(R16), .clk(clk), .clr(rst));
  Register #(.width(32)) registro17 (.D(wd), .en(decoder_1_out17), .Q(R17), .clk(clk), .clr(rst));
  Register #(.width(32)) registro18 (.D(wd), .en(decoder_1_out18), .Q(R18), .clk(clk), .clr(rst));
  Register #(.width(32)) registro19 (.D(wd), .en(decoder_1_out19), .Q(R19), .clk(clk), .clr(rst));
  Register #(.width(32)) registro20 (.D(wd), .en(decoder_1_out20), .Q(R20), .clk(clk), .clr(rst));
  Register #(.width(32)) registro21 (.D(wd), .en(decoder_1_out21), .Q(R21), .clk(clk), .clr(rst));
  Register #(.width(32)) registro22 (.D(wd), .en(decoder_1_out22), .Q(R22), .clk(clk), .clr(rst));
  Register #(.width(32)) registro23 (.D(wd), .en(decoder_1_out23), .Q(R23), .clk(clk), .clr(rst));
  Register #(.width(32)) registro24 (.D(wd), .en(decoder_1_out24), .Q(R24), .clk(clk), .clr(rst));
  Register #(.width(32)) registro25 (.D(wd), .en(decoder_1_out25), .Q(R25), .clk(clk), .clr(rst));
  Register #(.width(32)) registro26 (.D(wd), .en(decoder_1_out26), .Q(R26), .clk(clk), .clr(rst));
  Register #(.width(32)) registro27 (.D(wd), .en(decoder_1_out27), .Q(R27), .clk(clk), .clr(rst));
  Register #(.width(32)) registro28 (.D(wd), .en(decoder_1_out28), .Q(R28), .clk(clk), .clr(rst));
  Register #(.width(32)) registro29 (.D(wd), .en(decoder_1_out29), .Q(R29), .clk(clk), .clr(rst));
  Register #(.width(32)) registro30 (.D(wd), .en(decoder_1_out30), .Q(R30), .clk(clk), .clr(rst));
  Register #(.width(32)) registro31 (.D(wd), .en(decoder_1_out31), .Q(R31), .clk(clk), .clr(rst));
  Multiplexer #(.select(5), .width(32)) multiplexer_1 (
    .in0(R0), .in1(R1), .in2(R2), .in3(R3), .in4(R4), .in5(R5), .in6(R6), .in7(R7), .in8(R8), .in9(R9),
    .in10(R10), .in11(R11), .in12(R12), .in13(R13), .in14(R14), .in15(R15), .in16(R16), .in17(R17),
    .in18(R18), .in19(R19), .in20(R20), .in21(R21), .in22(R22), .in23(R23), .in24(R24), .in25(R25),
    .in26(R26), .in27(R27), .in28(R28), .in29(R29), .in30(R30), .in31(R31), .out(A), .sel(rs));
  Multiplexer #(.select(5), .width(32)) multiplexer_2 (
    .in0(R0), .in1(R1), .in2(R2), .in3(R3), .in4(R4), .in5(R5), .in6(R6), .in7(R7), .in8(R8), .in9(R9),
    .in10(R10), .in11(R11), .in12(R12), .in13(R13), .in14(R14), .in15(R15), .in16(R16), .in17(R17),
    .in18(R18), .in19(R19), .in20(R20), .in21(R21), .in22(R22), .in23(R23), .in24(R24), .in25(R25),
    .in26(R26), .in27(R27), .in28(R28), .in29(R29), .in30(R30), .in31(R31), .out(B), .sel(rt));
endmodule

module mem_instrucciones (
  input  [31:0] PC,
  output [31:0] INSTR
);

  ROM #(.addrWidth(12), .dataWidth(32)) ROM_instrucciones_e2f7ba31 (.addr(PC[11:0]), .data(INSTR));

  // Notes on the sheet:
  //   contents of ROM_instrucciones_e2f7ba31 (hex, n*v repeats v):
  //   20080200 0 0 0 2009020a 0 0 0 ad090000 0 0 0 81040000 0 0 0 20050100 0 0 0 c000012 0 0 0 20060300 0
  //   0 0 acc20000 0 0 0 20050100 0 0 0 c000036 0 0 0 acc20004 0 0 0 acc30008 0 0 0 8cd30000 0 0 0
  //   8cd40004 0 0 0 8cd50008 0 0 0 20080120 0 0 0 8d160004 0 0 0 8000011 0 0 0 23bdfff4 0 0 0 afbf0008 0
  //   0 0 afb10004 0 0 0 afb20000 0 0 0 20110000 0 0 0 20120001 0 0 0 20080000 0 0 0 a05820 0 0 0 104482a
  //   0 0 0 11200014 0 0 0 1100000a 0 0 0 200a0001 0 0 0 110a000c 0 0 0 2525020 0 0 0 1515020 0 0 0
  //   2408820 0 0 0 1409020 0 0 0 ad6a0000 0 0 0 216b0004 0 0 0 21080001 0 0 0 800001a 0 0 0 ad600000 0 0
  //   0 216b0004 0 0 0 21080001 0 0 0 800001a 0 0 0 200a0001 0 0 0 ad6a0000 0 0 0 216b0004 0 0 0 21080001
  //   0 0 0 800001a 0 0 0 2401020 0 0 0 8fbf0008 0 0 0 8fb10004 0 0 0 8fb20000 0 0 0 23bd000c 0 0 0
  //   3e00008 0 0 0 23bdfffc 0 0 0 afbf0000 0 0 0 20020000 0 0 0 20030000 0 0 0 20080000 0 0 0 a05820 0 0
  //   0 104482a 0 0 0 11200006 0 0 0 816a0000 0 0 0 4a1020 0 0 0 20630001 0 0 0 216b0004 0 0 0 21080001 0
  //   0 0 800003c 0 0 0 8fbf0000 0 0 0 23bd0004 0 0 0 3e00008
endmodule

module unidad_control (
  input  [5:0] opcode,
  input  [5:0] funct,
  output RegDst,
  output ALUSrc,
  output MemtoReg0,
  output MemtoReg1,
  output RegWrite,
  output MemRead,
  output MemWrite,
  output Branch,
  output Jump,
  output Jal,
  output Jr,
  output ALUOp0,
  output ALUOp1
);

  wire [15:13] ROM_de_control_9a8f4c43_data;

  ROM #(.addrWidth(12), .dataWidth(16)) ROM_de_control_9a8f4c43 (
    .addr({opcode, funct}),
    .data({ROM_de_control_9a8f4c43_data, ALUOp1, ALUOp0, Jr, Jal, Jump, Branch, MemWrite, MemRead, RegWrite, MemtoReg1, MemtoReg0, ALUSrc, RegDst}));

  // Notes on the sheet:
  //   contents of ROM_de_control_9a8f4c43 (hex, n*v repeats v):
  //   8*1011 400 55*1011 64*0 64*100 64*31c 64*880 192*0 64*12 1472*0 64*3a 128*0 64*36 448*0 64*42
endmodule

module control_alu (
  input  [1:0] ALUOp,
  input  [5:0] funct,
  output [2:0] op
);

  ROM #(.dataWidth(3)) ROM_control_ALU_7f4686d9 (.addr({ALUOp, funct}), .data(op));

  // Notes on the sheet:
  //   contents of ROM_control_ALU_7f4686d9 (hex, n*v repeats v):
  //   64*0 64*1 34*0 1 0 2 3 0 4 0 0 5
endmodule

module mem_datos (
  input  [31:0] addr,
  input  [31:0] din,
  input  we,
  input  oe,
  input  clk,
  output [31:0] dout,
  output [31:0] lb
);

  wire [7:0] bitselector_1_out;

  RAM #(.addrWidth(12), .asyncread("true"), .dataWidth(32)) Memoria_de_datos_d02892b9 (
    .addr(addr[13:2]), .we(we), .oe(oe), .clk(clk), .din(din), .dout(dout));
  BitSelector #(.group(8), .width(32)) bitselector_1 (.in(dout), .out(bitselector_1_out), .sel(addr[1:0]));
  assign lb = {{24{bitselector_1_out[7]}}, bitselector_1_out};  // Bit_Extender bit_extender_1
endmodule

module proximo_pc (
  input  [31:0] pc4,
  input  [31:0] imm32,
  input  [25:0] target,
  input  [31:0] a_val,
  input  Branch,
  input  zero_flag,
  input  [1:0] pc_sel,
  output [31:0] pc_next
);

  wire Branch_Zero_94673aa2_out;
  wire [31:0] adder_1_out, and_1_out, bit_extender_1_out, multiplexer_1_out, or_1_out, shifter_1_out,
       shifter_2_out;

  Shifter #(.width(32)) shifter_1 (.in(imm32), .\dist (5'b00010), .out(shifter_1_out));
  and Branch_Zero_94673aa2 (Branch_Zero_94673aa2_out, Branch, zero_flag);
  assign bit_extender_1_out = {{6{1'b0}}, target};  // Bit_Extender bit_extender_1
  Adder #(.width(32)) adder_1 (.a(pc4), .b(shifter_1_out), .out(adder_1_out), .cin(1'b0));  // open: cout
  Shifter #(.width(32)) shifter_2 (.in(bit_extender_1_out), .\dist (5'b00010), .out(shifter_2_out));
  Multiplexer #(.width(32)) multiplexer_1 (
    .in0(pc4), .in1(adder_1_out), .out(multiplexer_1_out), .sel(Branch_Zero_94673aa2_out));
  assign and_1_out = pc4 & 32'hf0000000;  // AND_Gate and_1, 32 bits wide
  assign or_1_out = shifter_2_out | and_1_out;  // OR_Gate or_1, 32 bits wide
  Multiplexer #(.select(2), .width(32)) multiplexer_2 (
    .in0(multiplexer_1_out), .in1(or_1_out), .in2(a_val), .in3(a_val), .out(pc_next), .sel(pc_sel));
endmodule

module main (
  input  RST,
  output [31:0] PC,
  output [31:0] INSTR,
  output [31:0] A,
  output [31:0] B,
  output [31:0] ALU,
  output [31:0] W,
  output [31:0] MEM,
  output [31:0] R0,
  output [31:0] R1,
  output [31:0] R2,
  output [31:0] R3,
  output [31:0] R4,
  output [31:0] R5,
  output [31:0] R6,
  output [31:0] R7,
  output [31:0] R8,
  output [31:0] R9,
  output [31:0] R10,
  output [31:0] R11,
  output [31:0] R12,
  output [31:0] R13,
  output [31:0] R14,
  output [31:0] R15,
  output [31:0] R16,
  output [31:0] R17,
  output [31:0] R18,
  output [31:0] R19,
  output [31:0] R20,
  output [31:0] R21,
  output [31:0] R22,
  output [31:0] R23,
  output [31:0] R24,
  output [31:0] R25,
  output [31:0] R26,
  output [31:0] R27,
  output [31:0] R28,
  output [31:0] R29,
  output [31:0] R30,
  output [31:0] R31
);

  wire alu32_1_z, clock_1_out, unidad_control_1_alusrc, unidad_control_1_branch, unidad_control_1_memread,
       unidad_control_1_memwrite, unidad_control_1_regwrite;
  wire [1:0] unidad_control_1_aluop0, unidad_control_1_jump, unidad_control_1_memtoreg0,
       unidad_control_1_regdst;
  wire [2:0] control_alu_1_op;
  wire [4:0] wr;
  wire [31:0] adder_1_out, bit_extender_1_out, mem_datos_1_lb, multiplexer_2_out, proximo_pc_1_pc_next;

  Clock clock_1 (.out(clock_1_out));
  Register #(.width(32)) Registro_PC_ff24f707 (
    .D(proximo_pc_1_pc_next), .en(1'b1), .Q(PC), .clk(clock_1_out), .clr(RST));
  Adder #(.width(32)) adder_1 (.a(PC), .b(32'h4), .out(adder_1_out), .cin(1'b0));  // open: cout
  banco_registros banco_registros_1 (
    .rs(INSTR[25:21]), .rt(INSTR[20:16]), .wr(wr), .wd(W), .we(unidad_control_1_regwrite), .clk(clock_1_out),
    .rst(RST), .A(A), .B(B), .R0(R0), .R1(R1), .R2(R2), .R3(R3), .R4(R4), .R5(R5), .R6(R6), .R7(R7), .R8(R8),
    .R9(R9), .R10(R10), .R11(R11), .R12(R12), .R13(R13), .R14(R14), .R15(R15), .R16(R16), .R17(R17),
    .R18(R18), .R19(R19), .R20(R20), .R21(R21), .R22(R22), .R23(R23), .R24(R24), .R25(R25), .R26(R26),
    .R27(R27), .R28(R28), .R29(R29), .R30(R30), .R31(R31));
  mem_instrucciones mem_instrucciones_1 (.PC(PC), .INSTR(INSTR));
  unidad_control unidad_control_1 (
    .opcode(INSTR[31:26]), .funct(INSTR[5:0]), .RegDst(unidad_control_1_regdst[0]),
    .ALUSrc(unidad_control_1_alusrc), .MemtoReg0(unidad_control_1_memtoreg0[0]),
    .MemtoReg1(unidad_control_1_memtoreg0[1]), .RegWrite(unidad_control_1_regwrite),
    .MemRead(unidad_control_1_memread), .MemWrite(unidad_control_1_memwrite),
    .Branch(unidad_control_1_branch), .Jump(unidad_control_1_jump[0]), .Jal(unidad_control_1_regdst[1]),
    .Jr(unidad_control_1_jump[1]), .ALUOp0(unidad_control_1_aluop0[0]), .ALUOp1(unidad_control_1_aluop0[1]));
  control_alu control_alu_1 (.ALUOp(unidad_control_1_aluop0), .funct(INSTR[5:0]), .op(control_alu_1_op));
  assign bit_extender_1_out = {{16{INSTR[15]}}, INSTR[15:0]};  // Bit_Extender bit_extender_1
  Multiplexer #(.select(2), .width(5)) multiplexer_1 (
    .in0(INSTR[20:16]), .in1(INSTR[15:11]), .in2({5{1'b1}}), .in3({5{1'b1}}), .out(wr),
    .sel(unidad_control_1_regdst));
  Multiplexer #(.width(32)) multiplexer_2 (
    .in0(B), .in1(bit_extender_1_out), .out(multiplexer_2_out), .sel(unidad_control_1_alusrc));
  proximo_pc proximo_pc_1 (
    .pc4(adder_1_out), .imm32(bit_extender_1_out), .target(INSTR[25:0]), .a_val(A),
    .Branch(unidad_control_1_branch), .zero_flag(alu32_1_z), .pc_sel(unidad_control_1_jump),
    .pc_next(proximo_pc_1_pc_next));
  alu32 alu32_1 (.A(A), .B(multiplexer_2_out), .OP(control_alu_1_op), .R(ALU), .Z(alu32_1_z));
  mem_datos mem_datos_1 (
    .addr(ALU), .din(B), .we(unidad_control_1_memwrite), .oe(unidad_control_1_memread), .clk(clock_1_out),
    .dout(MEM), .lb(mem_datos_1_lb));
  Multiplexer #(.select(2), .width(32)) multiplexer_3 (
    .in0(ALU), .in1(MEM), .in2(mem_datos_1_lb), .in3(adder_1_out), .out(W), .sel(unidad_control_1_memtoreg0));

  // Other names for the same wires on the sheet: a_val[31:0] = A; alu_res[31:0] = ALU; b_val[31:0] = B;
  //   rs[4:0] = INSTR[25:21]; mem_rdata[31:0] = MEM; wr_data[31:0] = W
endmodule
